# Fritzing sketch nodemcu_pir_sensor (saved by Fritzing 0.9.3b)

parts:
  PIR1 = PIR sensor
  U1 = NodeMCU V1.0 [part_number=1]

nets:
  VDD: PIR1.VDD, U1.3V3
  N1: PIR1.SIG, U1.D8
  GND: PIR1.GND, U1.GND

custom parts:
  NodeMCU V1.0: ESP8266 based NodeMCU
